# Fritzing sketch BoardLayout (saved by Fritzing 0.9.4)
breadboards: 1
perfboards: 1

parts:
  M1 = STM32F103C8T6 blue mini board
  J2 = Dagu DGServo 9g header (male) [package=THT]
  J3 = Dagu DGServo 9g header (male) [package=THT]
  J4 = Dagu DGServo 9g header (male) [package=THT]
  J5 = Dagu DGServo 9g header (male) [package=THT]
  J6 = Dagu DGServo 9g header (male) [package=THT]
  J7 = Dagu DGServo 9g header (male) [package=THT]
  J8 = Dagu DGServo 9g header (male) [package=THT]
  J9 = Dagu DGServo 9g header (male) [package=THT]
  J10 = Dagu DGServo 9g header (male) [package=THT]
  J11 = Dagu DGServo 9g header (male) [package=THT]
  J12 = Dagu DGServo 9g header (male) [package=THT]
  J13 = Dagu DGServo 9g header (male) [package=THT]
  J14 = Dagu DGServo 9g header (male) [package=THT]
  J15 = Dagu DGServo 9g header (male) [package=THT]
  J16 = Dagu DGServo 9g header (male) [package=THT]
  5_volt_supply = Power plug
  J17 = Dagu DGServo 9g header (male) [package=THT]
  J18 = Dagu DGServo 9g header (male) [package=THT]
  J19 = Dagu DGServo 9g header (male) [package=THT]
  J20 = Dagu DGServo 9g header (male) [package=THT]
  J21 = Dagu DGServo 9g header (male) [package=THT]
  J22 = Dagu DGServo 9g header (male) [package=THT]
  J23 = Dagu DGServo 9g header (male) [package=THT]
  J24 = Dagu DGServo 9g header (male) [package=THT]
  J25 = Dagu DGServo 9g header (male) [package=THT]
  J26 = Dagu DGServo 9g header (male) [package=THT]
  J27 = Dagu DGServo 9g header (male) [package=THT]
  J28 = Dagu DGServo 9g header (male) [package=THT]
  J29 = Dagu DGServo 9g header (male) [package=THT]
  J30 = Dagu DGServo 9g header (male) [package=THT]
  J31 = Dagu DGServo 9g header (male) [package=THT]

nets:
  VCC: M1.5V, J2.Vcc, J3.Vcc, J4.Vcc, J5.Vcc, J6.Vcc, J7.Vcc, J8.Vcc, J9.Vcc, J10.Vcc, J11.Vcc, J12.Vcc, J13.Vcc, J14.Vcc, J15.Vcc, J16.Vcc, 5_volt_supply.VCC, J17.Vcc, J18.Vcc, J19.Vcc, J20.Vcc, J21.Vcc, J22.Vcc, J23.Vcc, J24.Vcc, J25.Vcc, J26.Vcc, J27.Vcc, J28.Vcc, J29.Vcc, J30.Vcc, J31.Vcc
  GND: M1.G, M1.GND, J2.gnd, J3.gnd, J4.gnd, J5.gnd, J6.gnd, J7.gnd, J8.gnd, J9.gnd, J10.gnd, J11.gnd, J12.gnd, J13.gnd, J14.gnd, J15.gnd, J16.gnd, 5_volt_supply.GND, J17.gnd, J18.gnd, J19.gnd, J20.gnd, J21.gnd, J22.gnd, J23.gnd, J24.gnd, J25.gnd, J26.gnd, J27.gnd, J28.gnd, J29.gnd, J30.gnd, J31.gnd
  N1: M1.B11, J3.pulse
